# Fritzing sketch Ardurail_RS232_Booster (saved by Fritzing 0.7.5b)
breadboards: 1

parts:
  Arduino1 = Arduino
  C1 = Electrolytic Capacitor [capacitance=10µF voltage=16V package="100 mil [THT, electrolytic]"]
  IC2 = IC, DIP package, 20 pins [chip_label=MAX233 spacing=300mil]
  C3 = Ceramic Capacitor [capacitance=0.47mF voltage=16V package="100 mil [THT, multilayer]"]
  Q1 = NPN-Transistor [part_number=BC547 package="TO92 [THT]"]
  R1 = Resistor [tolerance=±5% resistance=1k package=THT]
  R2 = Resistor [tolerance=±5% resistance=1k package=THT]
  D1 = Rectifier Diode [part_number=1N4001 package="300 mil [THT]"]

nets:
  N1: Arduino1.D7, IC2.pin20
  N2: Arduino1.D6, R2.Pin_1
  N3: Arduino1.+5V, C1.+, IC2.pin6, IC2.pin9
  N4: Arduino1.GND, C1.-
  N5: IC2.pin1, Q1.C
  N6: IC2.pin8, IC2.pin13
  N7: IC2.pin10, IC2.pin11, IC2.pin16
  N8: IC2.pin12, IC2.pin17
  N9: IC2.pin18, C3.0, D1.cathode
  N10: Q1.E, R2.Pin_0
  N11: Q1.B, R1.Pin_0

notes:
  S88-Bus
  A0: Data
  A1: Clock
  A2: PS
  A3: Reset
  Pins 11, 12, 13 are reserved for Ethernet- shield!
  Booster
  Inputs RS232 level (Tams B-2)
  - Go (Button)
  - Shortcut
  - Signal
  Do not use pin2! The IRQ for pin 2 is needed inside Maerklino!!!
  Datasheets and information:
  http://www.tams-online.de/htmls/produkte/b2/B-2_D.PDF
  http://www.tams-online.de/bilder/faq/faq_b2_large.gif
  http://datasheets.maximintegrated.com/en/ds/MAX220-MAX249.pdf
  USE THIS ON YOUR OWN RISK!!!!
