# Fritzing sketch Ardurail_TTL_Booster (saved by Fritzing 0.7.5b)
breadboards: 1

parts:
  Arduino1 = Arduino
  Q1 = NPN-Transistor [package="TO92 [THT]"]
  R1 = Resistor [tolerance=±5% resistance=220 package=THT]

nets:
  N1: Arduino1.D7, Q1.E, R1.Pin_0
  N2: Arduino1.+5V, Q1.C
  N3: Arduino1.GND, R1.Pin_1

notes:
  S88-Bus
  A0: Data
  A1: Clock
  A2: PS
  A3: Reset
  Pins 11, 12, 13 are reserved for Ethernet- shield!
  Booster
  Inputs TTL level
  - Go
  - Shortcut
  - Signal
  USE THIS ON YOUR OWN RISK!!!!
  Do not use pin2! The IRQ for pin 2 is needed inside Maerklino!!!
